// Logisim project DELA ROSA_Project 1.circ as structural Verilog: 10 circuits, main circuit Main
module Main (
  input  [3:0] in_1,
  input  [3:0] in_2,
  input  in_3,
  input  [1:0] in_4
);

  wire bcd_to_7_segment_converter_1_a_2, bcd_to_7_segment_converter_1_b_2, bcd_to_7_segment_converter_1_c_2,
       bcd_to_7_segment_converter_1_d_2, bcd_to_7_segment_converter_1_e, bcd_to_7_segment_converter_1_f,
       bcd_to_7_segment_converter_1_g, bcd_to_7_segment_converter_2_a_2, bcd_to_7_segment_converter_2_b_2,
       bcd_to_7_segment_converter_2_c_2, bcd_to_7_segment_converter_2_d_2, bcd_to_7_segment_converter_2_e,
       bcd_to_7_segment_converter_2_f, bcd_to_7_segment_converter_2_g, bcd_to_7_segment_converter_3_a_2,
       bcd_to_7_segment_converter_3_b_2, bcd_to_7_segment_converter_3_c_2, bcd_to_7_segment_converter_3_d_2,
       bcd_to_7_segment_converter_3_e, bcd_to_7_segment_converter_3_f, bcd_to_7_segment_converter_3_g,
       bcd_to_7_segment_converter_4_a_2, bcd_to_7_segment_converter_4_b_2, bcd_to_7_segment_converter_4_c_2,
       bcd_to_7_segment_converter_4_d_2, bcd_to_7_segment_converter_4_e, bcd_to_7_segment_converter_4_f,
       bcd_to_7_segment_converter_4_g, bcd_to_7_segment_converter_5_a_2, bcd_to_7_segment_converter_5_b_2,
       bcd_to_7_segment_converter_5_c_2, bcd_to_7_segment_converter_5_d_2, bcd_to_7_segment_converter_5_e,
       bcd_to_7_segment_converter_5_f, bcd_to_7_segment_converter_5_g, bcd_to_7_segment_converter_6_a_2,
       bcd_to_7_segment_converter_6_b_2, bcd_to_7_segment_converter_6_c_2, bcd_to_7_segment_converter_6_d_2,
       bcd_to_7_segment_converter_6_e, bcd_to_7_segment_converter_6_f, bcd_to_7_segment_converter_6_g,
       bcd_to_7_segment_converter_7_a_2, bcd_to_7_segment_converter_7_b_2, bcd_to_7_segment_converter_7_c_2,
       bcd_to_7_segment_converter_7_d_2, bcd_to_7_segment_converter_7_e, bcd_to_7_segment_converter_7_f,
       bcd_to_7_segment_converter_7_g;
  wire [3:0] comparator_1_out_9, operation_selection_1_out_4, operation_selection_1_out_5,
       operation_selection_1_out_6, operation_selection_1_out_7;
  wire [4:0] bit_extender_1_out, unsigned_addition_1_out_9;
  wire [6:0] base_selection_1_out_5, base_selection_1_out_6, base_selection_1_out_7;
  wire [27:0] base_7_converter_1_out_8, binary_converter_1_out_8, octal_converter_1_out_8,
       output_selection_1_out_5;

  BCD_to_7_segment_Converter bcd_to_7_segment_converter_1 (
    .A(output_selection_1_out_5[27]), .B(output_selection_1_out_5[26]), .C(output_selection_1_out_5[25]),
    .D(output_selection_1_out_5[24]), .a_2(bcd_to_7_segment_converter_1_a_2),
    .f(bcd_to_7_segment_converter_1_f), .b_2(bcd_to_7_segment_converter_1_b_2),
    .g(bcd_to_7_segment_converter_1_g), .c_2(bcd_to_7_segment_converter_1_c_2),
    .d_2(bcd_to_7_segment_converter_1_d_2), .e(bcd_to_7_segment_converter_1_e));
  Hex_Digit_Display hex_digit_display_1 (.value(in_1));  // open: dp
  _7_Segment_Display u_7_segment_display_1 (
    .g(bcd_to_7_segment_converter_1_g), .f(bcd_to_7_segment_converter_1_f),
    .a(bcd_to_7_segment_converter_1_a_2), .b(bcd_to_7_segment_converter_1_b_2),
    .e(bcd_to_7_segment_converter_1_e), .d(bcd_to_7_segment_converter_1_d_2),
    .c(bcd_to_7_segment_converter_1_c_2));  // open: dp
  Hex_Digit_Display hex_digit_display_2 (.value(in_2));  // open: dp
  BCD_to_7_segment_Converter bcd_to_7_segment_converter_2 (
    .A(output_selection_1_out_5[23]), .B(output_selection_1_out_5[22]), .C(output_selection_1_out_5[21]),
    .D(output_selection_1_out_5[20]), .a_2(bcd_to_7_segment_converter_2_a_2),
    .f(bcd_to_7_segment_converter_2_f), .b_2(bcd_to_7_segment_converter_2_b_2),
    .g(bcd_to_7_segment_converter_2_g), .c_2(bcd_to_7_segment_converter_2_c_2),
    .d_2(bcd_to_7_segment_converter_2_d_2), .e(bcd_to_7_segment_converter_2_e));
  _7_Segment_Display u_7_segment_display_2 (
    .g(bcd_to_7_segment_converter_2_g), .f(bcd_to_7_segment_converter_2_f),
    .a(bcd_to_7_segment_converter_2_a_2), .b(bcd_to_7_segment_converter_2_b_2),
    .e(bcd_to_7_segment_converter_2_e), .d(bcd_to_7_segment_converter_2_d_2),
    .c(bcd_to_7_segment_converter_2_c_2));  // open: dp
  Operation_Selection operation_selection_1 (
    .Operand_A(in_1), .Operand_B(in_2), .in_3(in_3), .out_4(operation_selection_1_out_4),
    .out_5(operation_selection_1_out_5), .out_6(operation_selection_1_out_6),
    .out_7(operation_selection_1_out_7));
  Unsigned_Addition unsigned_addition_1 (
    .Operand_A(operation_selection_1_out_4[0]), .in_2(operation_selection_1_out_4[1]),
    .in_3(operation_selection_1_out_4[2]), .in_4(operation_selection_1_out_4[3]),
    .Operand_B(operation_selection_1_out_6[0]), .in_6(operation_selection_1_out_6[1]),
    .in_7(operation_selection_1_out_6[2]), .in_8(operation_selection_1_out_6[3]),
    .out_9(unsigned_addition_1_out_9[0]), .out_10(unsigned_addition_1_out_9[1]),
    .out_11(unsigned_addition_1_out_9[2]), .out_12(unsigned_addition_1_out_9[3]),
    .out_13(unsigned_addition_1_out_9[4]));
  BCD_to_7_segment_Converter bcd_to_7_segment_converter_3 (
    .A(output_selection_1_out_5[19]), .B(output_selection_1_out_5[18]), .C(output_selection_1_out_5[17]),
    .D(output_selection_1_out_5[16]), .a_2(bcd_to_7_segment_converter_3_a_2),
    .f(bcd_to_7_segment_converter_3_f), .b_2(bcd_to_7_segment_converter_3_b_2),
    .g(bcd_to_7_segment_converter_3_g), .c_2(bcd_to_7_segment_converter_3_c_2),
    .d_2(bcd_to_7_segment_converter_3_d_2), .e(bcd_to_7_segment_converter_3_e));
  Comparator comparator_1 (
    .Operand_A(operation_selection_1_out_5[0]), .in_2(operation_selection_1_out_5[1]),
    .in_3(operation_selection_1_out_5[2]), .in_4(operation_selection_1_out_5[3]),
    .Operand_B(operation_selection_1_out_7[0]), .in_6(operation_selection_1_out_7[1]),
    .in_7(operation_selection_1_out_7[2]), .in_8(operation_selection_1_out_7[3]),
    .out_9(comparator_1_out_9[0]), .out_10(comparator_1_out_9[1]), .out_11(comparator_1_out_9[2]),
    .out_12(comparator_1_out_9[3]));
  _7_Segment_Display u_7_segment_display_3 (
    .g(bcd_to_7_segment_converter_3_g), .f(bcd_to_7_segment_converter_3_f),
    .a(bcd_to_7_segment_converter_3_a_2), .b(bcd_to_7_segment_converter_3_b_2),
    .e(bcd_to_7_segment_converter_3_e), .d(bcd_to_7_segment_converter_3_d_2),
    .c(bcd_to_7_segment_converter_3_c_2));  // open: dp
  assign bit_extender_1_out = {{1{1'b0}}, comparator_1_out_9};  // Bit_Extender bit_extender_1
  BCD_to_7_segment_Converter bcd_to_7_segment_converter_4 (
    .A(output_selection_1_out_5[15]), .B(output_selection_1_out_5[14]), .C(output_selection_1_out_5[13]),
    .D(output_selection_1_out_5[12]), .a_2(bcd_to_7_segment_converter_4_a_2),
    .f(bcd_to_7_segment_converter_4_f), .b_2(bcd_to_7_segment_converter_4_b_2),
    .g(bcd_to_7_segment_converter_4_g), .c_2(bcd_to_7_segment_converter_4_c_2),
    .d_2(bcd_to_7_segment_converter_4_d_2), .e(bcd_to_7_segment_converter_4_e));
  Base_Selection base_selection_1 (
    .in_1(unsigned_addition_1_out_9), .in_2(bit_extender_1_out), .in_3(in_3), .in_4(in_4),
    .out_5(base_selection_1_out_5), .out_6(base_selection_1_out_6), .out_7(base_selection_1_out_7));
  _7_Segment_Display u_7_segment_display_4 (
    .g(bcd_to_7_segment_converter_4_g), .f(bcd_to_7_segment_converter_4_f),
    .a(bcd_to_7_segment_converter_4_a_2), .b(bcd_to_7_segment_converter_4_b_2),
    .e(bcd_to_7_segment_converter_4_e), .d(bcd_to_7_segment_converter_4_d_2),
    .c(bcd_to_7_segment_converter_4_c_2));  // open: dp
  BCD_to_7_segment_Converter bcd_to_7_segment_converter_5 (
    .A(output_selection_1_out_5[11]), .B(output_selection_1_out_5[10]), .C(output_selection_1_out_5[9]),
    .D(output_selection_1_out_5[8]), .a_2(bcd_to_7_segment_converter_5_a_2),
    .f(bcd_to_7_segment_converter_5_f), .b_2(bcd_to_7_segment_converter_5_b_2),
    .g(bcd_to_7_segment_converter_5_g), .c_2(bcd_to_7_segment_converter_5_c_2),
    .d_2(bcd_to_7_segment_converter_5_d_2), .e(bcd_to_7_segment_converter_5_e));
  Binary_Converter binary_converter_1 (
    .LSB(base_selection_1_out_5[0]), .in_2(base_selection_1_out_5[1]), .in_3(base_selection_1_out_5[2]),
    .in_4(base_selection_1_out_5[3]), .in_5(base_selection_1_out_5[4]), .in_6(base_selection_1_out_5[5]),
    .MSB(base_selection_1_out_5[6]), .out_8(binary_converter_1_out_8));
  Octal_Converter octal_converter_1 (
    .LSB(base_selection_1_out_6[0]), .in_2(base_selection_1_out_6[1]), .in_3(base_selection_1_out_6[2]),
    .in_4(base_selection_1_out_6[3]), .in_5(base_selection_1_out_6[4]), .in_6(base_selection_1_out_6[5]),
    .in_7(base_selection_1_out_6[6]), .out_8(octal_converter_1_out_8));
  _7_Segment_Display u_7_segment_display_5 (
    .g(bcd_to_7_segment_converter_5_g), .f(bcd_to_7_segment_converter_5_f),
    .a(bcd_to_7_segment_converter_5_a_2), .b(bcd_to_7_segment_converter_5_b_2),
    .e(bcd_to_7_segment_converter_5_e), .d(bcd_to_7_segment_converter_5_d_2),
    .c(bcd_to_7_segment_converter_5_c_2));  // open: dp
  Base_7_Converter base_7_converter_1 (
    .MSB(base_selection_1_out_7[6]), .in_2(base_selection_1_out_7[5]), .E(base_selection_1_out_7[4]),
    .D(base_selection_1_out_7[3]), .C(base_selection_1_out_7[2]), .B(base_selection_1_out_7[1]),
    .A(base_selection_1_out_7[0]), .out_8(base_7_converter_1_out_8));
  BCD_to_7_segment_Converter bcd_to_7_segment_converter_6 (
    .A(output_selection_1_out_5[7]), .B(output_selection_1_out_5[6]), .C(output_selection_1_out_5[5]),
    .D(output_selection_1_out_5[4]), .a_2(bcd_to_7_segment_converter_6_a_2),
    .f(bcd_to_7_segment_converter_6_f), .b_2(bcd_to_7_segment_converter_6_b_2),
    .g(bcd_to_7_segment_converter_6_g), .c_2(bcd_to_7_segment_converter_6_c_2),
    .d_2(bcd_to_7_segment_converter_6_d_2), .e(bcd_to_7_segment_converter_6_e));
  Output_Selection output_selection_1 (
    .in_1(binary_converter_1_out_8), .in_2(octal_converter_1_out_8), .in_3(base_7_converter_1_out_8),
    .in_4(in_4), .out_5(output_selection_1_out_5));
  _7_Segment_Display u_7_segment_display_6 (
    .g(bcd_to_7_segment_converter_6_g), .f(bcd_to_7_segment_converter_6_f),
    .a(bcd_to_7_segment_converter_6_a_2), .b(bcd_to_7_segment_converter_6_b_2),
    .e(bcd_to_7_segment_converter_6_e), .d(bcd_to_7_segment_converter_6_d_2),
    .c(bcd_to_7_segment_converter_6_c_2));  // open: dp
  BCD_to_7_segment_Converter bcd_to_7_segment_converter_7 (
    .A(output_selection_1_out_5[3]), .B(output_selection_1_out_5[2]), .C(output_selection_1_out_5[1]),
    .D(output_selection_1_out_5[0]), .a_2(bcd_to_7_segment_converter_7_a_2),
    .f(bcd_to_7_segment_converter_7_f), .b_2(bcd_to_7_segment_converter_7_b_2),
    .g(bcd_to_7_segment_converter_7_g), .c_2(bcd_to_7_segment_converter_7_c_2),
    .d_2(bcd_to_7_segment_converter_7_d_2), .e(bcd_to_7_segment_converter_7_e));
  _7_Segment_Display u_7_segment_display_7 (
    .g(bcd_to_7_segment_converter_7_g), .f(bcd_to_7_segment_converter_7_f),
    .a(bcd_to_7_segment_converter_7_a_2), .b(bcd_to_7_segment_converter_7_b_2),
    .e(bcd_to_7_segment_converter_7_e), .d(bcd_to_7_segment_converter_7_d_2),
    .c(bcd_to_7_segment_converter_7_c_2));  // open: dp

  // Notes on the sheet:
  //   OUTPUT:
  //   Operand A
  //   Operation Selector
  //   Output Base Selector
  //   MSD
  //   BCD to 7-segment
  //   Operand B
  //   BCD to 7-segment
  //   Operation
  //   Selection
  //   Unsigned Addition
  //   BCD to 7-segment
  //   Comparator
  //   BCD to 7-segment
  //   Base Selection
  //   Binary Converter
  //   Octal Converter
  //   BCD to 7-segment
  //   Base-7 Converter
  //   BCD to 7-segment
  //   Output Selection
  //   BCD to 7-segment
  //   LSD
endmodule

module Comparator (
  input  Operand_A,
  input  in_2,
  input  in_3,
  input  in_4,
  input  Operand_B,
  input  in_6,
  input  in_7,
  input  in_8,
  output out_9,
  output out_10,
  output out_11,
  output out_12
);

  wire [2:0] comparator_1_gt;

  Comparator_part #(.width(4), .mode("unsigned")) comparator_1 (
    .a({in_4, in_3, in_2, Operand_A}), .b({in_8, in_7, in_6, Operand_B}), .gt(comparator_1_gt[0]),
    .eq(comparator_1_gt[1]), .lt(comparator_1_gt[2]));
  Multiplexer #(.select(3), .width(4)) multiplexer_1 (
    .in1({in_4, in_3, in_2, Operand_A}), .in2(4'b0000), .in4({in_8, in_7, in_6, Operand_B}),
    .out({out_12, out_11, out_10, out_9}), .sel(comparator_1_gt), .en(1'b1));  // open: in0, in3, in5, in6, in7
endmodule

module Operation_Selection (
  input  [3:0] Operand_A,
  input  [3:0] Operand_B,
  input  in_3,
  output [3:0] out_4,
  output [3:0] out_5,
  output [3:0] out_6,
  output [3:0] out_7
);

  Demultiplexer #(.width(4)) demultiplexer_1 (.out0(out_4), .out1(out_5), .in(Operand_A), .sel(in_3), .en(1'b1));
  Demultiplexer #(.width(4)) demultiplexer_2 (.out0(out_6), .out1(out_7), .in(Operand_B), .sel(in_3), .en(1'b1));

  // Notes on the sheet:
  //   Operation Selector
endmodule

module Unsigned_Addition (
  input  Operand_A,
  input  in_2,
  input  in_3,
  input  in_4,
  input  Operand_B,
  input  in_6,
  input  in_7,
  input  in_8,
  output out_9,
  output out_10,
  output out_11,
  output out_12,
  output out_13
);

  Adder #(.width(4)) adder_1 (
    .a({in_4, in_3, in_2, Operand_A}), .b({in_8, in_7, in_6, Operand_B}),
    .out({out_12, out_11, out_10, out_9}), .cout(out_13));  // open: cin
endmodule

module Base_Selection (
  input  [4:0] in_1,
  input  [4:0] in_2,
  input  in_3,
  input  [1:0] in_4,
  output [6:0] out_5,
  output [6:0] out_6,
  output [6:0] out_7
);

  wire [4:0] multiplexer_1_out;
  wire [6:0] bit_extender_1_out;

  assign bit_extender_1_out = {{2{1'b0}}, multiplexer_1_out};  // Bit_Extender bit_extender_1
  Multiplexer #(.width(5)) multiplexer_1 (.in0(in_1), .in1(in_2), .out(multiplexer_1_out), .sel(in_3), .en(1'b1));
  Demultiplexer #(.select(2), .width(7)) demultiplexer_1 (
    .out0(out_5), .out1(out_6), .out2(out_7), .in(bit_extender_1_out), .sel(in_4), .en(1'b1));  // open: out3

  // Notes on the sheet:
  //   Output of Unsigned Addition
  //   Output of Comparator
  //   Operation Selector
  //   Output Base Selector
endmodule

module BCD_to_7_segment_Converter (
  input  A,
  input  B,
  input  C,
  input  D,
  output a_2,
  output f,
  output b_2,
  output g,
  output c_2,
  output d_2,
  output e
);

  wire and_1_out, and_2_out, and_3_out, and_4_out, and_5_out, and_6_out, and_7_out, and_8_out, and_9_out,
       and_10_out, and_11_out, and_12_out, and_13_out, and_14_out, not_1_out, not_2_out, not_3_out,
       not_4_out, not_5_out, not_6_out, not_7_out, not_8_out, not_9_out, not_10_out, not_11_out, not_12_out,
       not_13_out, not_14_out, not_15_out, not_16_out, not_17_out, not_18_out, not_19_out, not_20_out,
       not_21_out, or_2_out, or_3_out, or_4_out;

  not not_1 (not_1_out, B);
  not not_2 (not_2_out, D);
  not not_3 (not_3_out, C);
  not not_4 (not_4_out, D);
  not not_5 (not_5_out, C);
  not not_6 (not_6_out, D);
  not not_7 (not_7_out, C);
  not not_8 (not_8_out, D);
  not not_9 (not_9_out, B);
  not not_10 (not_10_out, C);
  not not_11 (not_11_out, D);
  not not_12 (not_12_out, C);
  not not_13 (not_13_out, B);
  not not_14 (not_14_out, D);
  not not_15 (not_15_out, B);
  not not_16 (not_16_out, D);
  not not_17 (not_17_out, C);
  not not_18 (not_18_out, D);
  not not_19 (not_19_out, B);
  not not_20 (not_20_out, D);
  and and_1 (and_1_out, not_1_out, not_2_out);
  and and_2 (and_2_out, B, D);
  and and_3 (and_3_out, not_3_out, not_4_out);
  and and_4 (and_4_out, B, not_5_out);
  and and_5 (and_5_out, B, not_6_out);
  not not_21 (not_21_out, B);
  and and_6 (and_6_out, not_7_out, not_8_out);
  and and_7 (and_7_out, C, D);
  and and_8 (and_8_out, not_9_out, C);
  and and_9 (and_9_out, B, not_10_out);
  and and_10 (and_10_out, B, not_11_out);
  or or_1 (c_2, not_12_out, D, B);
  and and_11 (and_11_out, not_13_out, not_14_out);
  and and_12 (and_12_out, not_15_out, C);
  and and_13 (and_13_out, C, not_16_out);
  and and_14 (and_14_out, B, not_17_out, D);
  or or_2 (or_2_out, B, C, not_18_out);
  or or_3 (or_3_out, A, not_19_out, C);
  or or_4 (or_4_out, A, not_20_out);
  or or_5 (a_2, and_1_out, C, and_2_out, A);
  or or_6 (f, and_3_out, and_4_out, and_5_out, A);
  or or_7 (b_2, not_21_out, and_6_out, and_7_out);
  or or_8 (g, and_8_out, and_9_out, and_10_out, A);
  or or_9 (d_2, and_11_out, and_12_out, and_13_out, and_14_out, A);
  and and_15 (e, or_2_out, or_3_out, or_4_out);

  // Notes on the sheet:
  //   MSB
  //   LSB
endmodule

module Binary_Converter (
  input  LSB,
  input  in_2,
  input  in_3,
  input  in_4,
  input  in_5,
  input  in_6,
  input  MSB,
  output [27:0] out_8
);

  assign out_8[3:0] = {{3{1'b0}}, LSB};  // Bit_Extender bit_extender_1
  assign out_8[7:4] = {{3{1'b0}}, in_2};  // Bit_Extender bit_extender_2
  assign out_8[11:8] = {{3{1'b0}}, in_3};  // Bit_Extender bit_extender_3
  assign out_8[15:12] = {{3{1'b0}}, in_4};  // Bit_Extender bit_extender_4
  assign out_8[19:16] = {{3{1'b0}}, in_5};  // Bit_Extender bit_extender_5
  assign out_8[23:20] = {{3{1'b0}}, in_6};  // Bit_Extender bit_extender_6
  assign out_8[27:24] = {{3{1'b0}}, MSB};  // Bit_Extender bit_extender_7
endmodule

module Output_Selection (
  input  [27:0] in_1,
  input  [27:0] in_2,
  input  [27:0] in_3,
  input  [1:0] in_4,
  output [27:0] out_5
);

  Multiplexer #(.select(2), .width(28)) multiplexer_1 (
    .in0(in_1), .in1(in_2), .in2(in_3), .in3({28{1'b0}}), .out(out_5), .sel(in_4));  // open: en

  // Notes on the sheet:
  //   octal
  //   binary
  //   base-7
  //   Outpu Base Selector
endmodule

module Octal_Converter (
  input  LSB,
  input  in_2,
  input  in_3,
  input  in_4,
  input  in_5,
  input  in_6,
  input  in_7,
  output [27:0] out_8
);

  assign out_8[3:0] = {{1{1'b0}}, {in_3, in_2, LSB}};  // Bit_Extender bit_extender_1
  assign out_8[7:4] = {{1{1'b0}}, {in_6, in_5, in_4}};  // Bit_Extender bit_extender_2
  assign out_8[11:8] = {{1{1'b0}}, {2'b00, in_7}};  // Bit_Extender bit_extender_3

  assign out_8[27:12] = {16{1'b0}};

  // Notes on the sheet:
  //   MSB
endmodule

module Base_7_Converter (
  input  MSB,
  input  in_2,
  input  E,
  input  D,
  input  C,
  input  B,
  input  A,
  output [27:0] out_8
);

  wire and_2_out, and_3_out, and_4_out, and_5_out, and_6_out, and_7_out, and_8_out, and_9_out, and_10_out,
       and_11_out, and_12_out, and_13_out, and_14_out, and_15_out, and_16_out, and_17_out, and_18_out,
       and_19_out, and_20_out, and_21_out, and_22_out, and_23_out, and_24_out, and_25_out, and_26_out,
       and_27_out, and_28_out, and_29_out, and_30_out, and_31_out, and_32_out, not_1_out, not_2_out,
       not_3_out, not_4_out, not_5_out, not_6_out, not_7_out, not_8_out, not_9_out, not_10_out, not_11_out,
       not_12_out, not_13_out, not_14_out, not_15_out, not_16_out, not_17_out, not_18_out, not_19_out,
       not_20_out, not_21_out, not_22_out, not_23_out, not_24_out, not_25_out, not_26_out, not_27_out,
       not_28_out, not_29_out, not_30_out, not_31_out, not_32_out, not_33_out, not_34_out, not_35_out,
       not_36_out, not_37_out, not_38_out, not_39_out, not_40_out, not_41_out, not_42_out, not_43_out,
       not_44_out, not_45_out, not_46_out, not_47_out, not_48_out, not_49_out, not_50_out, not_51_out,
       not_52_out;

  and and_1 (out_8[6], E, D, C);
  not not_1 (not_1_out, E);
  not not_2 (not_2_out, D);
  not not_3 (not_3_out, C);
  not not_4 (not_4_out, D);
  not not_5 (not_5_out, E);
  not not_6 (not_6_out, B);
  not not_7 (not_7_out, C);
  not not_8 (not_8_out, D);
  not not_9 (not_9_out, D);
  not not_10 (not_10_out, E);
  not not_11 (not_11_out, D);
  not not_12 (not_12_out, A);
  not not_13 (not_13_out, E);
  not not_14 (not_14_out, B);
  not not_15 (not_15_out, D);
  not not_16 (not_16_out, B);
  not not_17 (not_17_out, A);
  not not_18 (not_18_out, C);
  not not_19 (not_19_out, C);
  not not_20 (not_20_out, C);
  not not_21 (not_21_out, E);
  not not_22 (not_22_out, D);
  not not_23 (not_23_out, C);
  not not_24 (not_24_out, E);
  not not_25 (not_25_out, D);
  not not_26 (not_26_out, A);
  not not_27 (not_27_out, E);
  not not_28 (not_28_out, C);
  not not_29 (not_29_out, A);
  not not_30 (not_30_out, E);
  not not_31 (not_31_out, B);
  not not_32 (not_32_out, D);
  not not_33 (not_33_out, C);
  not not_34 (not_34_out, B);
  not not_35 (not_35_out, D);
  not not_36 (not_36_out, B);
  not not_37 (not_37_out, A);
  not not_38 (not_38_out, C);
  not not_39 (not_39_out, B);
  not not_40 (not_40_out, A);
  not not_41 (not_41_out, E);
  not not_42 (not_42_out, D);
  not not_43 (not_43_out, B);
  not not_44 (not_44_out, D);
  not not_45 (not_45_out, C);
  not not_46 (not_46_out, E);
  not not_47 (not_47_out, B);
  not not_48 (not_48_out, A);
  not not_49 (not_49_out, C);
  not not_50 (not_50_out, A);
  not not_51 (not_51_out, D);
  not not_52 (not_52_out, A);
  and and_2 (and_2_out, not_1_out, D, C, B);
  and and_3 (and_3_out, E, not_2_out);
  and and_4 (and_4_out, E, not_3_out);
  and and_5 (and_5_out, not_4_out, C, B, A);
  and and_6 (and_6_out, not_5_out, D, not_6_out);
  and and_7 (and_7_out, D, not_7_out);
  and and_8 (and_8_out, E, not_8_out, C, A);
  and and_9 (and_9_out, E, not_9_out, C, B);
  and and_10 (and_10_out, not_10_out, not_11_out, C, not_12_out);
  and and_11 (and_11_out, not_13_out, C, not_14_out);
  and and_12 (and_12_out, not_15_out, C, not_16_out, not_17_out);
  and and_13 (and_13_out, D, not_18_out, B, A);
  and and_14 (and_14_out, E, not_19_out, B);
  and and_15 (and_15_out, E, D, not_20_out, A);
  and and_16 (and_16_out, not_21_out, not_22_out, not_23_out, B);
  and and_17 (and_17_out, not_24_out, not_25_out, B, not_26_out);
  and and_18 (and_18_out, not_27_out, not_28_out, B, not_29_out);
  and and_19 (and_19_out, not_30_out, D, not_31_out, A);
  and and_20 (and_20_out, E, not_32_out, not_33_out, not_34_out);
  and and_21 (and_21_out, E, not_35_out, not_36_out, not_37_out);
  and and_22 (and_22_out, E, not_38_out, not_39_out, not_40_out);
  and and_23 (and_23_out, E, C, B, A);
  and and_24 (and_24_out, E, D, B, A);
  and and_25 (and_25_out, E, D, C, B);
  and and_26 (and_26_out, not_41_out, not_42_out, not_43_out, A);
  and and_27 (and_27_out, not_44_out, not_45_out, A);
  and and_28 (and_28_out, not_46_out, D, not_47_out, not_48_out);
  and and_29 (and_29_out, D, not_49_out, not_50_out);
  and and_30 (and_30_out, D, C, B, A);
  and and_31 (and_31_out, E, not_51_out, C, B, not_52_out);
  and and_32 (and_32_out, E, D, C, A);
  or or_1 (out_8[5], and_2_out, and_3_out, and_4_out);
  or or_2 (out_8[4], and_5_out, and_6_out, and_7_out, and_8_out, and_9_out);
  or or_3 (out_8[2], and_10_out, and_11_out, and_12_out, and_13_out, and_14_out, and_15_out);
  or or_4 (out_8[1], and_16_out, and_17_out, and_18_out, and_19_out, and_20_out, and_21_out, and_22_out, and_23_out, and_24_out, and_25_out);
  or or_5 (out_8[0], and_26_out, and_27_out, and_28_out, and_29_out, and_30_out, and_31_out, and_32_out);

  assign {out_8[27:7], out_8[3]} = {22{1'b0}};

  // Notes on the sheet:
  //   LSB
endmodule
