// Logisim project 74LS682.circ as structural Verilog: 1 circuit, main circuit 74682
module _74682 (
  input  _20__Vcc,
  input  _2__A7,
  input  _3__B7,
  input  _18__B0,
  input  _4__A6,
  input  _17__A0,
  input  _5__B6,
  input  _16__B1,
  input  _6__A5,
  input  _15__A1,
  input  _7__B5,
  input  _14__B2,
  input  _8__A4,
  input  _13__A2,
  input  _9__B4,
  input  _12__B3,
  input  _10__GND,
  input  _11__A3,
  output _1__A___B,
  output _19__A___B
);

  wire and_1_out, and_2_out, and_3_out, and_4_out, and_5_out, and_6_out, and_7_out, and_8_out, not_1_out,
       not_2_out, not_3_out, not_4_out, not_5_out, not_6_out, not_7_out, not_8_out, not_9_out, not_10_out,
       not_11_out, not_12_out, not_13_out, not_14_out, not_15_out, not_16_out, not_17_out, not_18_out,
       not_19_out, not_20_out, not_21_out, not_22_out, not_23_out, not_24_out, xnor_1_out, xnor_2_out,
       xnor_3_out, xnor_4_out, xnor_5_out, xnor_6_out, xnor_7_out, xnor_8_out;

  not not_1 (not_1_out, _2__A7);
  not not_2 (not_2_out, _3__B7);
  not not_3 (not_3_out, _4__A6);
  not not_4 (not_4_out, _5__B6);
  not not_5 (not_5_out, _6__A5);
  not not_6 (not_6_out, _7__B5);
  not not_7 (not_7_out, _8__A4);
  not not_8 (not_8_out, _9__B4);
  not not_9 (not_9_out, _11__A3);
  not not_10 (not_10_out, _12__B3);
  not not_11 (not_11_out, _13__A2);
  not not_12 (not_12_out, _14__B2);
  not not_13 (not_13_out, _15__A1);
  not not_14 (not_14_out, _16__B1);
  not not_15 (not_15_out, _17__A0);
  not not_16 (not_16_out, _18__B0);
  xnor xnor_1 (xnor_1_out, not_1_out, not_2_out);
  xnor xnor_2 (xnor_2_out, not_3_out, not_4_out);
  xnor xnor_3 (xnor_3_out, not_5_out, not_6_out);
  xnor xnor_4 (xnor_4_out, not_7_out, not_8_out);
  xnor xnor_5 (xnor_5_out, not_9_out, not_10_out);
  xnor xnor_6 (xnor_6_out, not_11_out, not_12_out);
  xnor xnor_7 (xnor_7_out, not_13_out, not_14_out);
  xnor xnor_8 (xnor_8_out, not_15_out, not_16_out);
  not not_17 (not_17_out, not_15_out);
  not not_18 (not_18_out, not_13_out);
  not not_19 (not_19_out, not_11_out);
  not not_20 (not_20_out, not_9_out);
  not not_21 (not_21_out, not_7_out);
  not not_22 (not_22_out, not_5_out);
  not not_23 (not_23_out, not_3_out);
  not not_24 (not_24_out, not_1_out);
  and and_1 (and_1_out, xnor_1_out, xnor_2_out, xnor_3_out, xnor_4_out, xnor_5_out, xnor_6_out, xnor_7_out, not_16_out, not_17_out);
  and and_2 (and_2_out, xnor_1_out, xnor_2_out, xnor_3_out, xnor_4_out, xnor_5_out, xnor_6_out, not_14_out, not_18_out);
  and and_3 (and_3_out, xnor_1_out, xnor_2_out, xnor_3_out, xnor_4_out, xnor_5_out, not_12_out, not_19_out);
  and and_4 (and_4_out, xnor_1_out, xnor_2_out, xnor_3_out, xnor_4_out, not_10_out, not_20_out);
  and and_5 (and_5_out, xnor_1_out, xnor_2_out, xnor_3_out, not_8_out, not_21_out);
  and and_6 (and_6_out, xnor_1_out, xnor_2_out, not_6_out, not_22_out);
  and and_7 (and_7_out, xnor_1_out, not_4_out, not_23_out);
  and and_8 (and_8_out, not_2_out, not_24_out);
  nand nand_1 (_19__A___B, xnor_1_out, xnor_2_out, xnor_3_out, xnor_4_out, xnor_5_out, xnor_6_out, xnor_7_out, xnor_8_out);
  nor nor_1 (_1__A___B, and_1_out, and_2_out, and_3_out, and_4_out, and_5_out, and_6_out, and_7_out, and_8_out);

  // Notes on the sheet:
  //   74682: 8-bit magnitude comparator 
endmodule
