// Logisim project bcd.circ as structural Verilog: 1 circuit, main circuit main
module main (
  input  A,
  input  B,
  input  C,
  input  D,
  output out_5,
  output out_6,
  output out_7,
  output out_8,
  output out_9,
  output out_10,
  output out_11
);

  wire not_1_out, not_2_out, not_3_out, not_4_out, or_1_out, or_2_out, or_3_out, or_4_out, or_5_out,
       or_6_out, or_7_out, or_8_out, or_9_out, or_10_out, or_11_out, or_12_out, or_13_out, or_14_out,
       or_15_out, or_16_out, or_17_out, or_18_out, or_19_out, or_20_out, or_21_out, or_22_out, or_23_out,
       or_24_out, or_25_out;

  not not_1 (not_1_out, A);
  not not_2 (not_2_out, B);
  not not_3 (not_3_out, C);
  not not_4 (not_4_out, D);
  or or_1 (or_1_out, A, not_2_out, C, D);
  or or_2 (or_2_out, A, B, C, not_4_out);
  or or_3 (or_3_out, not_1_out, not_2_out, C, not_4_out);
  or or_4 (or_4_out, not_1_out, B, not_3_out, not_4_out);
  or or_5 (or_5_out, A, B, not_3_out, D);
  or or_6 (or_6_out, not_1_out, not_2_out, not_3_out);
  or or_7 (or_7_out, not_1_out, not_2_out, D);
  or or_8 (or_8_out, B, C, not_4_out);
  or or_9 (or_9_out, A, not_2_out, C);
  or or_10 (or_10_out, A, not_4_out);
  or or_11 (or_11_out, A, B, C);
  or or_12 (or_12_out, not_1_out, not_2_out, C, D);
  or or_13 (or_13_out, A, not_2_out, not_3_out, not_4_out);
  and and_1 (out_5, or_1_out, or_2_out, or_3_out, or_4_out);
  or or_14 (or_14_out, A, not_2_out, C, not_4_out);
  or or_15 (or_15_out, not_1_out, not_2_out, D);
  or or_16 (or_16_out, not_1_out, not_3_out, not_4_out);
  or or_17 (or_17_out, not_2_out, not_3_out, D);
  or or_18 (or_18_out, A, not_2_out, C, D);
  or or_19 (or_19_out, A, B, C, not_4_out);
  or or_20 (or_20_out, not_2_out, not_3_out, not_4_out);
  or or_21 (or_21_out, not_1_out, B, not_3_out, D);
  or or_22 (or_22_out, A, B, not_4_out);
  or or_23 (or_23_out, A, B, not_3_out);
  or or_24 (or_24_out, A, not_3_out, not_4_out);
  or or_25 (or_25_out, not_1_out, not_2_out, C, not_4_out);
  and and_2 (out_7, or_14_out, or_15_out, or_16_out, or_17_out);
  and and_3 (out_9, or_5_out, or_6_out, or_7_out);
  and and_4 (out_11, or_8_out, or_9_out, or_10_out);
  and and_5 (out_8, or_11_out, or_12_out, or_13_out);
  and and_6 (out_10, or_18_out, or_19_out, or_20_out, or_21_out);
  and and_7 (out_6, or_22_out, or_23_out, or_24_out, or_25_out);
endmodule
