// Logisim project PROJ 2.circ as structural Verilog: 5 circuits, main circuit main
module main (
  input  in_1
);

  wire n7_segment_display_driver_1_p4, n7_segment_display_driver_1_p5, n7_segment_display_driver_1_p6,
       n7_segment_display_driver_1_p7, n7_segment_display_driver_1_p8, n7_segment_display_driver_1_p9,
       n7_segment_display_driver_1_p10, n7_segment_display_driver_2_p6, n7_segment_display_driver_2_p7,
       n7_segment_display_driver_2_p8, n7_segment_display_driver_2_p9, n7_segment_display_driver_2_p10,
       n7_segment_display_driver_2_p11, n7_segment_display_driver_2_p12, n7_segment_display_driver_3_p4,
       n7_segment_display_driver_3_p5, n7_segment_display_driver_3_p6, n7_segment_display_driver_3_p7,
       n7_segment_display_driver_3_p8, n7_segment_display_driver_3_p9, n7_segment_display_driver_3_p10,
       n7_segment_display_driver_4_p5, n7_segment_display_driver_4_p6, n7_segment_display_driver_4_p7,
       n7_segment_display_driver_4_p8, n7_segment_display_driver_4_p9, n7_segment_display_driver_4_p10,
       n7_segment_display_driver_4_p11;
  wire [15:0] n7_segment_display_driver_4_p4;

  _7_Segment_Display u_7_segment_display_1 (
    .g(n7_segment_display_driver_1_p7), .f(n7_segment_display_driver_1_p5),
    .a(n7_segment_display_driver_1_p4), .b(n7_segment_display_driver_1_p6),
    .e(n7_segment_display_driver_1_p10), .d(n7_segment_display_driver_1_p9),
    .c(n7_segment_display_driver_1_p8));  // open: dp
  // _7_segment_display_driver 7_segment_display_driver_1: pin names not known; wires that end beside it: n7_segment_display_driver_4_p4[14], n7_segment_display_driver_4_p4[13], n7_segment_display_driver_4_p4[12], n7_segment_display_driver_1_p4, n7_segment_display_driver_1_p5, n7_segment_display_driver_1_p6, n7_segment_display_driver_1_p7, n7_segment_display_driver_1_p8, n7_segment_display_driver_1_p9, n7_segment_display_driver_1_p10
  // _7_segment_display_driver 7_segment_display_driver_2: pin names not known; wires that end beside it: n7_segment_display_driver_4_p4[15], n7_segment_display_driver_4_p4[11], n7_segment_display_driver_4_p4[10], n7_segment_display_driver_4_p4[9], n7_segment_display_driver_4_p4[8], n7_segment_display_driver_2_p6, n7_segment_display_driver_2_p7, n7_segment_display_driver_2_p8, n7_segment_display_driver_2_p9, n7_segment_display_driver_2_p10, n7_segment_display_driver_2_p11, n7_segment_display_driver_2_p12
  _7_Segment_Display u_7_segment_display_2 (
    .g(n7_segment_display_driver_2_p9), .f(n7_segment_display_driver_2_p7),
    .a(n7_segment_display_driver_2_p6), .b(n7_segment_display_driver_2_p8),
    .e(n7_segment_display_driver_2_p12), .d(n7_segment_display_driver_2_p11),
    .c(n7_segment_display_driver_2_p10));  // open: dp
  // _7_segment_display_driver 7_segment_display_driver_3: pin names not known; wires that end beside it: n7_segment_display_driver_4_p4[6], n7_segment_display_driver_4_p4[5], n7_segment_display_driver_4_p4[4], n7_segment_display_driver_3_p4, n7_segment_display_driver_3_p5, n7_segment_display_driver_3_p6, n7_segment_display_driver_3_p7, n7_segment_display_driver_3_p8, n7_segment_display_driver_3_p9, n7_segment_display_driver_3_p10
  _7_Segment_Display u_7_segment_display_3 (
    .g(n7_segment_display_driver_3_p7), .f(n7_segment_display_driver_3_p5),
    .a(n7_segment_display_driver_3_p4), .b(n7_segment_display_driver_3_p6),
    .e(n7_segment_display_driver_3_p10), .d(n7_segment_display_driver_3_p9),
    .c(n7_segment_display_driver_3_p8));  // open: dp
  // _7_segment_display_driver 7_segment_display_driver_4: pin names not known; wires that end beside it: n7_segment_display_driver_4_p4[3], n7_segment_display_driver_4_p4[2], n7_segment_display_driver_4_p4[1], n7_segment_display_driver_4_p4[0], n7_segment_display_driver_4_p5, n7_segment_display_driver_4_p6, n7_segment_display_driver_4_p7, n7_segment_display_driver_4_p8, n7_segment_display_driver_4_p9, n7_segment_display_driver_4_p10, n7_segment_display_driver_4_p11
  _7_Segment_Display u_7_segment_display_4 (
    .g(n7_segment_display_driver_4_p8), .f(n7_segment_display_driver_4_p6),
    .a(n7_segment_display_driver_4_p5), .b(n7_segment_display_driver_4_p7),
    .e(n7_segment_display_driver_4_p11), .d(n7_segment_display_driver_4_p10),
    .c(n7_segment_display_driver_4_p9));  // open: dp
  LED led_1 ();  // open: in
endmodule

module clocks_to_9 (
  input  in_1,
  output out_2,
  output out_3,
  output out_4,
  output out_5,
  output out_6
);

  wire d_ff_1_qn, d_ff_2_qn, d_ff_3_qn, d_ff_4_qn;

  D_Flip_Flop d_ff_1 (.clk(in_1), .D(d_ff_1_qn), .Q(out_2), .Qn(d_ff_1_qn), .reset(out_6));  // open: preset, en
  D_Flip_Flop d_ff_2 (.clk(d_ff_1_qn), .D(d_ff_2_qn), .Q(out_3), .Qn(d_ff_2_qn), .reset(out_6));  // open: preset, en
  D_Flip_Flop d_ff_3 (.clk(d_ff_2_qn), .D(d_ff_3_qn), .Q(out_4), .Qn(d_ff_3_qn), .reset(out_6));  // open: preset, en
  D_Flip_Flop d_ff_4 (.clk(d_ff_3_qn), .D(d_ff_4_qn), .Q(out_5), .Qn(d_ff_4_qn), .reset(out_6));  // open: preset, en
  and and_1 (out_6, out_3, out_5);
endmodule

module clocks_to_5 (
  input  in_1,
  output out_2,
  output out_3,
  output out_4,
  output out_5
);

  wire d_ff_1_qn, d_ff_2_qn, d_ff_3_qn;

  D_Flip_Flop d_ff_1 (.clk(in_1), .D(d_ff_1_qn), .Q(out_2), .Qn(d_ff_1_qn), .reset(out_5));  // open: preset, en
  D_Flip_Flop d_ff_2 (.clk(d_ff_1_qn), .D(d_ff_2_qn), .Q(out_3), .Qn(d_ff_2_qn), .reset(out_5));  // open: preset, en
  D_Flip_Flop d_ff_3 (.clk(d_ff_2_qn), .D(d_ff_3_qn), .Q(out_4), .Qn(d_ff_3_qn), .reset(out_5));  // open: preset, en
  and and_1 (out_5, out_3, out_4);
endmodule

module Stopwatch (
);

  wire clock_1_out, clocks_to_5_2_out_5, clocks_to_9_1_out_6, clocks_to_9_2_out_6,
       n7_segment_display_driver_1_p1, n7_segment_display_driver_1_p2, n7_segment_display_driver_1_p3,
       n7_segment_display_driver_1_p4, n7_segment_display_driver_1_p5, n7_segment_display_driver_1_p6,
       n7_segment_display_driver_1_p7, n7_segment_display_driver_2_p1, n7_segment_display_driver_2_p2,
       n7_segment_display_driver_2_p3, n7_segment_display_driver_2_p4, n7_segment_display_driver_2_p5,
       n7_segment_display_driver_2_p6, n7_segment_display_driver_2_p7, n7_segment_display_driver_3_p1,
       n7_segment_display_driver_3_p2, n7_segment_display_driver_3_p3, n7_segment_display_driver_3_p4,
       n7_segment_display_driver_3_p5, n7_segment_display_driver_3_p6, n7_segment_display_driver_3_p7,
       n7_segment_display_driver_4_p1, n7_segment_display_driver_4_p2, n7_segment_display_driver_4_p3,
       n7_segment_display_driver_4_p4, n7_segment_display_driver_4_p5, n7_segment_display_driver_4_p6,
       n7_segment_display_driver_4_p7;
  wire [2:0] clocks_to_5_1_out_2, clocks_to_5_2_out_2;
  wire [3:0] bit_extender_1_out, bit_extender_2_out, clocks_to_9_1_out_2, clocks_to_9_2_out_2;

  clocks_to_5 clocks_to_5_1 (
    .in_1(clocks_to_9_1_out_6), .out_2(clocks_to_5_1_out_2[0]), .out_3(clocks_to_5_1_out_2[1]),
    .out_4(clocks_to_5_1_out_2[2]));  // open: out_5
  assign bit_extender_1_out = {{1{1'b0}}, clocks_to_5_1_out_2};  // Bit_Extender bit_extender_1
  // _7_segment_display_driver 7_segment_display_driver_1: pin names not known; wires that end beside it: n7_segment_display_driver_1_p1, n7_segment_display_driver_1_p2, n7_segment_display_driver_1_p3, n7_segment_display_driver_1_p4, n7_segment_display_driver_1_p5, n7_segment_display_driver_1_p6, n7_segment_display_driver_1_p7
  _7_Segment_Display u_7_segment_display_1 (
    .g(n7_segment_display_driver_1_p7), .f(n7_segment_display_driver_1_p6),
    .a(n7_segment_display_driver_1_p1), .b(n7_segment_display_driver_1_p2),
    .e(n7_segment_display_driver_1_p5), .d(n7_segment_display_driver_1_p4), .c(n7_segment_display_driver_1_p3));  // open: dp
  clocks_to_9 clocks_to_9_1 (
    .in_1(clocks_to_5_2_out_5), .out_2(clocks_to_9_1_out_2[0]), .out_3(clocks_to_9_1_out_2[1]),
    .out_4(clocks_to_9_1_out_2[2]), .out_5(clocks_to_9_1_out_2[3]), .out_6(clocks_to_9_1_out_6));
  // _7_segment_display_driver 7_segment_display_driver_2: pin names not known; wires that end beside it: n7_segment_display_driver_2_p1, n7_segment_display_driver_2_p2, n7_segment_display_driver_2_p3, n7_segment_display_driver_2_p4, n7_segment_display_driver_2_p5, n7_segment_display_driver_2_p6, n7_segment_display_driver_2_p7
  _7_Segment_Display u_7_segment_display_2 (
    .g(n7_segment_display_driver_2_p7), .f(n7_segment_display_driver_2_p6),
    .a(n7_segment_display_driver_2_p1), .b(n7_segment_display_driver_2_p2),
    .e(n7_segment_display_driver_2_p5), .d(n7_segment_display_driver_2_p4), .c(n7_segment_display_driver_2_p3));  // open: dp
  clocks_to_5 clocks_to_5_2 (
    .in_1(clocks_to_9_2_out_6), .out_2(clocks_to_5_2_out_2[0]), .out_3(clocks_to_5_2_out_2[1]),
    .out_4(clocks_to_5_2_out_2[2]), .out_5(clocks_to_5_2_out_5));
  assign bit_extender_2_out = {{1{1'b0}}, clocks_to_5_2_out_2};  // Bit_Extender bit_extender_2
  // _7_segment_display_driver 7_segment_display_driver_3: pin names not known; wires that end beside it: n7_segment_display_driver_3_p1, n7_segment_display_driver_3_p2, n7_segment_display_driver_3_p3, n7_segment_display_driver_3_p4, n7_segment_display_driver_3_p5, n7_segment_display_driver_3_p6, n7_segment_display_driver_3_p7
  _7_Segment_Display u_7_segment_display_3 (
    .g(n7_segment_display_driver_3_p7), .f(n7_segment_display_driver_3_p6),
    .a(n7_segment_display_driver_3_p1), .b(n7_segment_display_driver_3_p2),
    .e(n7_segment_display_driver_3_p5), .d(n7_segment_display_driver_3_p4), .c(n7_segment_display_driver_3_p3));  // open: dp
  Clock clock_1 (.out(clock_1_out));
  clocks_to_9 clocks_to_9_2 (
    .in_1(clock_1_out), .out_2(clocks_to_9_2_out_2[0]), .out_3(clocks_to_9_2_out_2[1]),
    .out_4(clocks_to_9_2_out_2[2]), .out_5(clocks_to_9_2_out_2[3]), .out_6(clocks_to_9_2_out_6));
  // _7_segment_display_driver 7_segment_display_driver_4: pin names not known; wires that end beside it: n7_segment_display_driver_4_p1, n7_segment_display_driver_4_p2, n7_segment_display_driver_4_p3, n7_segment_display_driver_4_p4, n7_segment_display_driver_4_p5, n7_segment_display_driver_4_p6, n7_segment_display_driver_4_p7
  _7_Segment_Display u_7_segment_display_4 (
    .g(n7_segment_display_driver_4_p7), .f(n7_segment_display_driver_4_p6),
    .a(n7_segment_display_driver_4_p1), .b(n7_segment_display_driver_4_p2),
    .e(n7_segment_display_driver_4_p5), .d(n7_segment_display_driver_4_p4), .c(n7_segment_display_driver_4_p3));  // open: dp
endmodule

module Timer (
);

  wire clock_1_out, clocks_to_5_2_out_5, clocks_to_9_1_out_6, clocks_to_9_2_out_2, clocks_to_9_2_out_3,
       clocks_to_9_2_out_4, clocks_to_9_2_out_5, clocks_to_9_2_out_6, n7_segment_display_driver_1_p1,
       n7_segment_display_driver_1_p2, n7_segment_display_driver_1_p3, n7_segment_display_driver_1_p4,
       n7_segment_display_driver_1_p5, n7_segment_display_driver_1_p6, n7_segment_display_driver_1_p7,
       n7_segment_display_driver_2_p1, n7_segment_display_driver_2_p2, n7_segment_display_driver_2_p3,
       n7_segment_display_driver_2_p4, n7_segment_display_driver_2_p5, n7_segment_display_driver_2_p6,
       n7_segment_display_driver_2_p7, n7_segment_display_driver_3_p1, n7_segment_display_driver_3_p2,
       n7_segment_display_driver_3_p3, n7_segment_display_driver_3_p4, n7_segment_display_driver_3_p5,
       n7_segment_display_driver_3_p6, n7_segment_display_driver_3_p7, n7_segment_display_driver_4_p1,
       n7_segment_display_driver_4_p3, n7_segment_display_driver_4_p5, n7_segment_display_driver_4_p7,
       n7_segment_display_driver_4_p13, n7_segment_display_driver_4_p14, n7_segment_display_driver_4_p15,
       n7_segment_display_driver_4_p16, n7_segment_display_driver_4_p17, n7_segment_display_driver_4_p18,
       n7_segment_display_driver_4_p19;
  wire [2:0] clocks_to_5_1_out_2, clocks_to_5_2_out_2;
  wire [3:0] bit_extender_1_out, bit_extender_2_out, clocks_to_9_1_out_2;

  clocks_to_5 clocks_to_5_1 (
    .in_1(clocks_to_9_1_out_6), .out_2(clocks_to_5_1_out_2[0]), .out_3(clocks_to_5_1_out_2[1]),
    .out_4(clocks_to_5_1_out_2[2]));  // open: out_5
  assign bit_extender_1_out = {{1{1'b0}}, clocks_to_5_1_out_2};  // Bit_Extender bit_extender_1
  // _7_segment_display_driver 7_segment_display_driver_1: pin names not known; wires that end beside it: n7_segment_display_driver_1_p1, n7_segment_display_driver_1_p2, n7_segment_display_driver_1_p3, n7_segment_display_driver_1_p4, n7_segment_display_driver_1_p5, n7_segment_display_driver_1_p6, n7_segment_display_driver_1_p7
  _7_Segment_Display u_7_segment_display_1 (
    .g(n7_segment_display_driver_1_p7), .f(n7_segment_display_driver_1_p6),
    .a(n7_segment_display_driver_1_p1), .b(n7_segment_display_driver_1_p2),
    .e(n7_segment_display_driver_1_p5), .d(n7_segment_display_driver_1_p4), .c(n7_segment_display_driver_1_p3));  // open: dp
  clocks_to_9 clocks_to_9_1 (
    .in_1(clocks_to_5_2_out_5), .out_2(clocks_to_9_1_out_2[0]), .out_3(clocks_to_9_1_out_2[1]),
    .out_4(clocks_to_9_1_out_2[2]), .out_5(clocks_to_9_1_out_2[3]), .out_6(clocks_to_9_1_out_6));
  // _7_segment_display_driver 7_segment_display_driver_2: pin names not known; wires that end beside it: n7_segment_display_driver_2_p1, n7_segment_display_driver_2_p2, n7_segment_display_driver_2_p3, n7_segment_display_driver_2_p4, n7_segment_display_driver_2_p5, n7_segment_display_driver_2_p6, n7_segment_display_driver_2_p7
  _7_Segment_Display u_7_segment_display_2 (
    .g(n7_segment_display_driver_2_p7), .f(n7_segment_display_driver_2_p6),
    .a(n7_segment_display_driver_2_p1), .b(n7_segment_display_driver_2_p2),
    .e(n7_segment_display_driver_2_p5), .d(n7_segment_display_driver_2_p4), .c(n7_segment_display_driver_2_p3));  // open: dp
  clocks_to_5 clocks_to_5_2 (
    .in_1(clocks_to_9_2_out_6), .out_2(clocks_to_5_2_out_2[0]), .out_3(clocks_to_5_2_out_2[1]),
    .out_4(clocks_to_5_2_out_2[2]), .out_5(clocks_to_5_2_out_5));
  assign bit_extender_2_out = {{1{1'b0}}, clocks_to_5_2_out_2};  // Bit_Extender bit_extender_2
  // _7_segment_display_driver 7_segment_display_driver_3: pin names not known; wires that end beside it: n7_segment_display_driver_3_p1, n7_segment_display_driver_3_p2, n7_segment_display_driver_3_p3, n7_segment_display_driver_3_p4, n7_segment_display_driver_3_p5, n7_segment_display_driver_3_p6, n7_segment_display_driver_3_p7
  _7_Segment_Display u_7_segment_display_3 (
    .g(n7_segment_display_driver_3_p7), .f(n7_segment_display_driver_3_p6),
    .a(n7_segment_display_driver_3_p1), .b(n7_segment_display_driver_3_p2),
    .e(n7_segment_display_driver_3_p5), .d(n7_segment_display_driver_3_p4), .c(n7_segment_display_driver_3_p3));  // open: dp
  Clock clock_1 (.out(clock_1_out));
  clocks_to_9 clocks_to_9_2 (
    .in_1(clock_1_out), .out_2(clocks_to_9_2_out_2), .out_3(clocks_to_9_2_out_3),
    .out_4(clocks_to_9_2_out_4), .out_5(clocks_to_9_2_out_5), .out_6(clocks_to_9_2_out_6));
  // _7_segment_display_driver 7_segment_display_driver_4: pin names not known; wires that end beside it: n7_segment_display_driver_4_p1, clocks_to_9_2_out_2, n7_segment_display_driver_4_p3, clocks_to_9_2_out_3, n7_segment_display_driver_4_p5, clocks_to_9_2_out_4, n7_segment_display_driver_4_p7, clocks_to_9_2_out_5, n7_segment_display_driver_4_p1, n7_segment_display_driver_4_p3, n7_segment_display_driver_4_p5, n7_segment_display_driver_4_p7, n7_segment_display_driver_4_p13, n7_segment_display_driver_4_p14, n7_segment_display_driver_4_p15, n7_segment_display_driver_4_p16, n7_segment_display_driver_4_p17, n7_segment_display_driver_4_p18, n7_segment_display_driver_4_p19
  _7_Segment_Display u_7_segment_display_4 (
    .g(n7_segment_display_driver_4_p19), .f(n7_segment_display_driver_4_p18),
    .a(n7_segment_display_driver_4_p13), .b(n7_segment_display_driver_4_p14),
    .e(n7_segment_display_driver_4_p17), .d(n7_segment_display_driver_4_p16),
    .c(n7_segment_display_driver_4_p15));  // open: dp
endmodule
