// Logisim project cs20lab10_2.circ as structural Verilog: 1 circuit, main circuit main
module main (
  input  [3:0] A3_A2_A1_A0,
  output O0,
  output O1,
  output O2,
  output O3,
  output O4,
  output O5,
  output O6,
  output O7
);

  ROM #(.addrWidth(4)) rom_1 (.addr(A3_A2_A1_A0), .data({O7, O6, O5, O4, O3, O2, O1, O0}));  // open: sel

  // Notes on the sheet:
  //   contents of rom_1 (hex, n*v repeats v):
  //   0 80 80 80
endmodule
