// Logisim project cs20lab10_3.circ as structural Verilog: 1 circuit, main circuit main
module main (
  input  [3:0] A3_A2_A1_A0,
  output O0,
  output O1,
  output O2,
  output O3,
  output O4,
  output O5,
  output O6,
  output O7
);

  wire n7_segment_display_driver_1_p5, n7_segment_display_driver_1_p6, n7_segment_display_driver_1_p7,
       n7_segment_display_driver_1_p8, n7_segment_display_driver_1_p9, n7_segment_display_driver_1_p10,
       n7_segment_display_driver_1_p11;

  ROM #(.addrWidth(4)) rom_1 (.addr(A3_A2_A1_A0), .data({O7, O6, O5, O4, O3, O2, O1, O0}));  // open: sel
  // _7_segment_display_driver 7_segment_display_driver_1: pin names not known; wires that end beside it: O0, O1, O2, O3, n7_segment_display_driver_1_p5, n7_segment_display_driver_1_p6, n7_segment_display_driver_1_p7, n7_segment_display_driver_1_p8, n7_segment_display_driver_1_p9, n7_segment_display_driver_1_p10, n7_segment_display_driver_1_p11
  _7_Segment_Display u_7_segment_display_1 (
    .g(n7_segment_display_driver_1_p11), .f(n7_segment_display_driver_1_p10),
    .a(n7_segment_display_driver_1_p5), .b(n7_segment_display_driver_1_p6),
    .e(n7_segment_display_driver_1_p9), .d(n7_segment_display_driver_1_p8), .c(n7_segment_display_driver_1_p7));  // open: dp

  // Notes on the sheet:
  //   contents of rom_1 (hex, n*v repeats v):
  //   5*0 8 4 c 0 4 2 6 0 c 6 9
endmodule
