// Logisim project cs20labrep3a.circ as structural Verilog: 1 circuit, main circuit main
module main (
);

  wire transistor_1_out;

  Transistor #(.\type ("n")) transistor_1 (.in(1'b1), .out(transistor_1_out), .gate(1'b0));
  LED led_1 (.in(transistor_1_out));

  // Notes on the sheet:
  //   power source
  //   gate
  //   ground
  //   LED
endmodule
