// Logisim project cs20labrep3b.circ as structural Verilog: 1 circuit, main circuit main
module main (
  input  input__0,
  input  input__0_2
);

  wire transistor_1_out, transistor_4_out, transistor_5_out;

  Transistor transistor_1 (.in(1'b1), .out(transistor_1_out), .gate(input__0_2));
  Transistor transistor_2 (.in(1'b1), .out(transistor_1_out), .gate(input__0));
  Transistor #(.\type ("n")) transistor_3 (.in(transistor_4_out), .out(transistor_1_out), .gate(input__0));
  Transistor #(.\type ("n")) transistor_4 (.in(1'b0), .out(transistor_4_out), .gate(input__0_2));
  Transistor transistor_5 (.in(1'b1), .out(transistor_5_out), .gate(transistor_1_out));
  LED led_1 (.in(transistor_5_out));
  Transistor #(.\type ("n")) transistor_6 (.in(1'b0), .out(transistor_5_out), .gate(transistor_1_out));

  // Notes on the sheet:
  //   NAND gate
  //   NOT gate
  //   output: 0
endmodule
