// Logisim project cs20labrep3c.circ as structural Verilog: 1 circuit, main circuit main
module main (
  input  input__1,
  input  input__0
);

  wire transistor_1_out, transistor_2_out, transistor_5_out;

  Transistor #(.\type ("n")) transistor_1 (.in(1'b0), .out(transistor_1_out), .gate(input__1));
  Transistor transistor_2 (.in(1'b1), .out(transistor_2_out), .gate(input__1));
  Transistor transistor_3 (.in(transistor_2_out), .out(transistor_1_out), .gate(input__0));
  Transistor #(.\type ("n")) transistor_4 (.in(1'b0), .out(transistor_1_out), .gate(input__0));
  Transistor transistor_5 (.in(1'b1), .out(transistor_5_out), .gate(transistor_1_out));
  LED led_1 (.in(transistor_5_out));
  Transistor #(.\type ("n")) transistor_6 (.in(1'b0), .out(transistor_5_out), .gate(transistor_1_out));

  // Notes on the sheet:
  //   NOR gate
  //   NOT gate
  //   output: 1
endmodule
