// Logisim project circuit.circ as structural Verilog: 1 circuit, main circuit main
module main (
);

  wire nand_1_out, nand_2_out, nand_3_out, not_1_out, not_2_out, not_3_out, not_4_out, or_1_out, or_2_out,
       or_3_out, undriven, undriven_2, undriven_3, undriven_4;

  nand nand_1 (nand_1_out, undriven_2, undriven_3);
  nand nand_2 (nand_2_out, undriven, undriven_4);
  not not_1 (not_1_out, undriven_4);
  not not_2 (not_2_out, nand_2_out);
  nand nand_3 (nand_3_out, undriven, nand_1_out);
  not not_3 (not_3_out, nand_3_out);
  or or_1 (or_1_out, not_1_out, undriven_3);
  not not_4 (not_4_out, or_1_out);
  or or_2 (or_2_out, not_3_out, not_4_out);
  or or_3 (or_3_out, not_2_out, or_2_out);

  // Notes on the sheet:
  //   A
  //   C
  //   D
  //   B
  //   Output
endmodule
