// Logisim project cs20lab4_1a.circ as structural Verilog: 1 circuit, main circuit main
module main (
  input  in_1,
  input  in_2
);

  wire n7432_1_p3;

  LED led_1 (.in(n7432_1_p3));
  // _7432 7432_1: pin names not known; wires that end beside it: in_1, in_2, n7432_1_p3, 1'b0, 1'b1
endmodule
