// Logisim project cs20lab4_2.circ as structural Verilog: 1 circuit, main circuit main
module main (
  input  A,
  input  B,
  input  C
);

  wire n7404_1_p1, n7432_1_p2, n7432_1_p3;

  LED led_1 (.in(n7432_1_p3));
  // _7432 7432_1: pin names not known; wires that end beside it: C, n7432_1_p2, n7432_1_p3, 1'b0, 1'b1, 1'b0
  // _7404 7404_1: pin names not known; wires that end beside it: n7404_1_p1, n7432_1_p2, 1'b1, 1'b0
  // _7400 7400_1: pin names not known; wires that end beside it: A, B, n7404_1_p1, 1'b1
endmodule
