// Logisim project cs20lab4_3.circ as structural Verilog: 1 circuit, main circuit main
module main (
  input  A,
  input  B,
  input  C,
  input  D
);

  wire n7400_1_p3, n7400_1_p6, n7400_1_p10, n7432_1_p1, n7432_1_p3, n7432_1_p4, n7432_1_p5, n7432_1_p6,
       n7432_1_p9, n7432_1_p10;

  LED led_1 (.in(n7432_1_p6));
  // _7432 7432_1: pin names not known; wires that end beside it: n7432_1_p1, D, n7432_1_p3, n7432_1_p4, n7432_1_p5, n7432_1_p6, 1'b0, 1'b1, n7432_1_p9, n7432_1_p10, n7432_1_p5
  // _7400 7400_1: pin names not known; wires that end beside it: A, B, n7400_1_p3, C, D, n7400_1_p6, 1'b1, A, n7400_1_p6, n7400_1_p10
  // _7404 7404_1: pin names not known; wires that end beside it: 1'b0, n7400_1_p3, n7432_1_p4, B, n7432_1_p1, 1'b0, 1'b1, n7400_1_p10, n7432_1_p10, n7432_1_p3, n7432_1_p9
endmodule
