// Logisim project A D WORKS.circ as structural Verilog: 1 circuit, main circuit main
module main (
  input  D,
  input  C,
  input  B,
  input  A
);

  wire n7402_1_p4, n7402_1_p6, n7402_1_p7, n7402_1_p12, n7402_1_p13, n7402_2_p2, n7402_2_p3, n7402_2_p4,
       n7402_2_p6, n7402_2_p10, n7402_4_p2, n7402_4_p6, n7402_4_p12, n7402_5_p2, n7402_5_p4, n7402_5_p5,
       n7402_5_p6, n7402_5_p7, n7402_5_p12, n7402_5_p13, n7402_6_p4, n7402_6_p6, n7402_6_p7, n7402_7_p3,
       n7402_7_p4, n7402_7_p5, n7402_8_p6, n7402_8_p7, n7402_8_p8, n7402_8_p12, n7402_9_p2, n7402_9_p6,
       n7402_9_p7, n7402_9_p8, n7402_9_p9, n7402_10_p2, n7402_10_p4, n7402_10_p6, n7402_11_p6, n7402_11_p7,
       n7402_12_p2, n7402_12_p6, n7402_12_p7, n7402_12_p9, n7402_12_p10, n7402_13_p4, n7402_13_p6,
       n7402_13_p7, n7402_14_p6, n7402_14_p7;

  // _7402 7402_1: pin names not known; wires that end beside it: 1'b0, D, D, n7402_1_p4, C, n7402_1_p6, n7402_1_p7, n7402_1_p6, n7402_1_p7, n7402_1_p6, n7402_1_p7, n7402_1_p12, n7402_1_p13, 1'b1
  // _7402 7402_2: pin names not known; wires that end beside it: 1'b0, n7402_2_p2, n7402_2_p3, n7402_2_p4, n7402_2_p3, n7402_2_p6, n7402_2_p2, n7402_2_p6, n7402_2_p6, n7402_2_p10, n7402_2_p4, 1'b1
  // _7402 7402_3: pin names not known
  // _7402 7402_4: pin names not known; wires that end beside it: 1'b0, n7402_4_p2, D, n7402_1_p4, D, n7402_4_p6, n7402_4_p2, n7402_4_p6, C, n7402_4_p6, C, n7402_4_p12, n7402_1_p4, 1'b1
  // _7402 7402_5: pin names not known; wires that end beside it: 1'b0, n7402_5_p2, n7402_1_p13, n7402_5_p4, n7402_5_p5, n7402_5_p6, n7402_5_p7, n7402_5_p6, n7402_5_p7, n7402_5_p6, n7402_5_p7, n7402_5_p12, n7402_5_p13, 1'b1
  // _7402 7402_6: pin names not known; wires that end beside it: 1'b0, n7402_1_p12, n7402_4_p2, n7402_6_p4, C, n7402_6_p6, n7402_6_p7, n7402_6_p6, n7402_6_p7, n7402_6_p6, n7402_6_p7, n7402_2_p3, n7402_5_p2, 1'b1
  // _7402 7402_7: pin names not known; wires that end beside it: 1'b0, n7402_2_p10, n7402_7_p3, n7402_7_p4, n7402_7_p5, n7402_7_p5, n7402_7_p3, 1'b1
  // _7402 7402_8: pin names not known; wires that end beside it: 1'b0, n7402_5_p12, n7402_5_p13, n7402_5_p12, n7402_5_p13, n7402_8_p6, n7402_8_p7, n7402_8_p8, n7402_8_p7, n7402_8_p8, n7402_8_p6, n7402_8_p12, n7402_8_p8, 1'b1
  // _7402 7402_9: pin names not known; wires that end beside it: 1'b0, n7402_9_p2, n7402_2_p3, n7402_9_p2, n7402_2_p3, n7402_9_p6, n7402_9_p7, n7402_9_p8, n7402_9_p9, n7402_9_p7, n7402_9_p9, n7402_9_p2, n7402_9_p8, 1'b1
  // _7402 7402_10: pin names not known; wires that end beside it: 1'b0, n7402_10_p2, B, n7402_10_p4, B, n7402_10_p6, n7402_10_p2, n7402_10_p6, A, n7402_10_p6, A, n7402_5_p4, n7402_10_p4, 1'b1
  // _7402 7402_11: pin names not known; wires that end beside it: 1'b0, B, B, n7402_10_p4, A, n7402_11_p6, n7402_11_p7, n7402_11_p6, n7402_11_p7, n7402_11_p6, n7402_11_p7, n7402_5_p5, n7402_6_p4, 1'b1
  // _7402 7402_12: pin names not known; wires that end beside it: 1'b0, n7402_12_p2, n7402_9_p6, n7402_12_p2, n7402_8_p12, n7402_12_p6, n7402_12_p7, n7402_12_p6, n7402_12_p9, n7402_12_p10, n7402_12_p9, n7402_7_p5, n7402_12_p10, 1'b1
  // _7402 7402_13: pin names not known; wires that end beside it: 1'b0, n7402_5_p2, n7402_1_p4, n7402_13_p4, n7402_5_p4, n7402_13_p6, n7402_13_p7, n7402_13_p6, n7402_13_p7, n7402_13_p6, n7402_13_p7, n7402_12_p9, n7402_12_p2, 1'b1
  // _7402 7402_14: pin names not known; wires that end beside it: 1'b0, n7402_4_p12, n7402_10_p2, n7402_5_p5, A, n7402_14_p6, n7402_14_p7, n7402_14_p6, n7402_14_p7, n7402_14_p6, n7402_14_p7, n7402_9_p9, n7402_13_p4, 1'b1
  _7_Segment_Display u_7_segment_display_1 (.a(n7402_12_p7), .d(n7402_7_p4));  // open: g, f, b, e, c, dp
  // _7402 7402_15: pin names not known

  // Notes on the sheet:
  //   (D+C’+B+A) (D+C+B+A’) 
  //   D'
  //   D'+C'
  //   D+C
  //   D+C'
  //   D'+C+B'+A'
  //   C'
  //   D+C+B+A'
  //   D'+C
  //   D+C'+B+A
  //   B'
  //   B+A
  //   B+A'
  //   A'
  //   B'+A'
  //   D'+C'+B+A'
  //   C'+B'+A'
  //   D'+C+B'+A
  //   B'+A
endmodule
