// Logisim project A WORKS.circ as structural Verilog: 1 circuit, main circuit main
module main (
  input  D,
  input  C,
  input  B,
  input  A
);

  wire n7402_1_p4, n7402_1_p6, n7402_1_p7, n7402_1_p12, n7402_1_p13, n7402_3_p2, n7402_3_p6, n7402_3_p12,
       n7402_4_p2, n7402_4_p4, n7402_4_p5, n7402_4_p6, n7402_4_p7, n7402_4_p12, n7402_4_p13, n7402_5_p4,
       n7402_5_p6, n7402_5_p7, n7402_5_p12, n7402_6_p6, n7402_6_p7, n7402_6_p8, n7402_6_p12, n7402_7_p2,
       n7402_7_p6, n7402_7_p7, n7402_7_p8, n7402_7_p9, n7402_8_p2, n7402_8_p4, n7402_8_p6, n7402_9_p6,
       n7402_9_p7, n7402_10_p4, n7402_11_p6, n7402_11_p7, n7402_11_p13, undriven;

  // _7402 7402_1: pin names not known; wires that end beside it: 1'b0, D, D, n7402_1_p4, C, n7402_1_p6, n7402_1_p7, n7402_1_p6, n7402_1_p7, n7402_1_p6, n7402_1_p7, n7402_1_p12, n7402_1_p13, 1'b1
  // _7402 7402_2: pin names not known
  // _7402 7402_3: pin names not known; wires that end beside it: 1'b0, n7402_3_p2, D, n7402_1_p4, D, n7402_3_p6, n7402_3_p2, n7402_3_p6, C, n7402_3_p6, C, n7402_3_p12, n7402_1_p4, 1'b1
  // _7402 7402_4: pin names not known; wires that end beside it: 1'b0, n7402_4_p2, n7402_1_p13, n7402_4_p4, n7402_4_p5, n7402_4_p6, n7402_4_p7, n7402_4_p6, n7402_4_p7, n7402_4_p6, n7402_4_p7, n7402_4_p12, n7402_4_p13, 1'b1
  // _7402 7402_5: pin names not known; wires that end beside it: 1'b0, n7402_1_p12, n7402_3_p2, n7402_5_p4, C, n7402_5_p6, n7402_5_p7, n7402_5_p6, n7402_5_p7, n7402_5_p6, n7402_5_p7, n7402_5_p12, n7402_4_p2, 1'b1
  // _7402 7402_6: pin names not known; wires that end beside it: 1'b0, n7402_4_p12, n7402_4_p13, n7402_4_p12, n7402_4_p13, n7402_6_p6, n7402_6_p7, n7402_6_p8, n7402_6_p7, n7402_6_p8, n7402_6_p6, n7402_6_p12, n7402_6_p8, 1'b1
  // _7402 7402_7: pin names not known; wires that end beside it: 1'b0, n7402_7_p2, n7402_5_p12, n7402_7_p2, n7402_5_p12, n7402_7_p6, n7402_7_p7, n7402_7_p8, n7402_7_p9, n7402_7_p7, n7402_7_p9, n7402_7_p2, n7402_7_p8, 1'b1
  // _7402 7402_8: pin names not known; wires that end beside it: 1'b0, n7402_8_p2, B, n7402_8_p4, B, n7402_8_p6, n7402_8_p2, n7402_8_p6, A, n7402_8_p6, A, n7402_4_p4, n7402_8_p4, 1'b1
  // _7402 7402_9: pin names not known; wires that end beside it: 1'b0, B, B, n7402_8_p4, A, n7402_9_p6, n7402_9_p7, n7402_9_p6, n7402_9_p7, n7402_9_p6, n7402_9_p7, n7402_4_p5, n7402_5_p4, 1'b1
  // _7402 7402_10: pin names not known; wires that end beside it: 1'b0, n7402_7_p6, n7402_6_p12, n7402_10_p4, 1'b1
  // _7402 7402_11: pin names not known; wires that end beside it: 1'b0, n7402_3_p12, n7402_8_p2, n7402_4_p5, A, n7402_11_p6, n7402_11_p7, n7402_11_p6, n7402_11_p7, n7402_11_p6, n7402_11_p7, n7402_7_p9, n7402_11_p13, n7402_11_p13, 1'b1
  _7_Segment_Display u_7_segment_display_1 (.a(n7402_10_p4), .d(undriven));  // open: g, f, b, e, c, dp
  // _7402 7402_12: pin names not known

  // Notes on the sheet:
  //   D'
  //   D'+C'
  //   D+C
  //   D+C'
  //   D'+C+B'+A'
  //   C'
  //   D+C+B+A'
  //   D'+C
  //   D+C'+B+A
  //   B'
  //   B+A
  //   B+A'
  //   A'
  //   B'+A'
  //   D'+C'+B+A'
  //   B'+A
endmodule
