// Logisim project cs20lab5.circ as structural Verilog: 1 circuit, main circuit main
module main (
  input  D,
  input  C,
  input  B,
  input  A
);

  wire n7402_1_p2, n7402_1_p3, n7402_1_p4, n7402_1_p6, n7402_1_p7, n7402_1_p12, n7402_1_p13, n7402_2_p4,
       n7402_2_p6, n7402_2_p7, n7402_2_p12, n7402_3_p2, n7402_3_p3, n7402_3_p4, n7402_3_p6, n7402_3_p10,
       n7402_4_p2, n7402_4_p5, n7402_4_p6, n7402_4_p9, n7402_4_p12, n7402_4_p13, n7402_5_p2, n7402_5_p6,
       n7402_6_p2, n7402_6_p4, n7402_6_p5, n7402_6_p6, n7402_6_p7, n7402_6_p12, n7402_6_p13, n7402_7_p2,
       n7402_7_p3, n7402_7_p6, n7402_7_p8, n7402_7_p12, n7402_8_p6, n7402_8_p7, n7402_8_p12, n7402_8_p13,
       n7402_9_p6, n7402_9_p7, n7402_10_p5, n7402_10_p6, n7402_10_p7, n7402_10_p9, n7402_11_p4, n7402_11_p7,
       n7402_11_p8, n7402_11_p10, n7402_11_p12, n7402_12_p6, n7402_12_p7, n7402_12_p8, n7402_12_p12,
       n7402_13_p6, n7402_13_p7, n7402_13_p12, n7402_13_p13, n7402_14_p6, n7402_14_p7, n7402_14_p11,
       n7402_14_p13, n7402_15_p2, n7402_15_p6, n7402_15_p7, n7402_15_p8, n7402_15_p9, n7402_16_p5,
       n7402_16_p6, n7402_16_p7, n7402_16_p12, n7402_16_p13, n7402_17_p5, n7402_17_p6, n7402_17_p9,
       n7402_17_p11, n7402_18_p4, n7402_18_p5, n7402_18_p6, n7402_18_p11, n7402_19_p6, n7402_20_p6,
       n7402_20_p7, n7402_21_p2, n7402_21_p6, n7402_21_p7, n7402_21_p9, n7402_21_p10, n7402_22_p6,
       n7402_22_p7, n7402_23_p6, n7402_23_p7, n7402_23_p12, n7402_23_p13, n7402_24_p6, n7402_24_p7,
       n7402_24_p10, n7402_24_p12, n7402_25_p6, n7402_25_p7, n7402_26_p2, n7402_26_p4, n7402_26_p6,
       n7402_27_p6, n7402_27_p7, n7402_27_p12, n7402_27_p13, n7402_28_p6, n7402_28_p7, n7402_28_p10,
       n7402_28_p11, n7402_29_p2, n7402_29_p4, n7402_29_p6, n7402_29_p8;

  // _7402 7402_1: pin names not known; wires that end beside it: 1'b0, n7402_1_p2, n7402_1_p3, n7402_1_p4, B, n7402_1_p6, n7402_1_p7, n7402_1_p6, n7402_1_p7, n7402_1_p6, n7402_1_p7, n7402_1_p12, n7402_1_p13, 1'b1
  // _7402 7402_2: pin names not known; wires that end beside it: 1'b0, D, D, n7402_2_p4, C, n7402_2_p6, n7402_2_p7, n7402_2_p6, n7402_2_p7, n7402_2_p6, n7402_2_p7, n7402_2_p12, n7402_1_p3, 1'b1
  // _7402 7402_3: pin names not known; wires that end beside it: 1'b0, n7402_3_p2, n7402_3_p3, n7402_3_p4, n7402_3_p3, n7402_3_p6, n7402_3_p2, n7402_3_p6, n7402_3_p6, n7402_3_p10, n7402_3_p4, 1'b1
  // _7402 7402_4: pin names not known; wires that end beside it: 1'b0, n7402_4_p2, n7402_1_p3, n7402_4_p2, n7402_4_p5, n7402_4_p6, n7402_4_p2, n7402_4_p6, n7402_4_p9, n7402_4_p6, n7402_4_p9, n7402_4_p12, n7402_4_p13, 1'b1
  // _7402 7402_5: pin names not known; wires that end beside it: 1'b0, n7402_5_p2, D, n7402_2_p4, D, n7402_5_p6, n7402_5_p2, n7402_5_p6, C, n7402_5_p6, C, n7402_1_p2, n7402_2_p4, 1'b1
  // _7402 7402_6: pin names not known; wires that end beside it: 1'b0, n7402_6_p2, n7402_1_p3, n7402_6_p4, n7402_6_p5, n7402_6_p6, n7402_6_p7, n7402_6_p6, n7402_6_p7, n7402_6_p6, n7402_6_p7, n7402_6_p12, n7402_6_p13, 1'b1
  // _7402 7402_7: pin names not known; wires that end beside it: 1'b0, n7402_7_p2, n7402_7_p3, n7402_7_p2, n7402_7_p3, n7402_7_p6, n7402_7_p2, n7402_7_p8, n7402_2_p12, n7402_7_p8, n7402_6_p5, n7402_7_p12, n7402_7_p3, 1'b1
  // _7402 7402_8: pin names not known; wires that end beside it: 1'b0, n7402_1_p12, n7402_1_p13, n7402_1_p12, n7402_1_p13, n7402_8_p6, n7402_8_p7, n7402_2_p12, n7402_8_p7, n7402_6_p4, n7402_8_p6, n7402_8_p12, n7402_8_p13, 1'b1
  // _7402 7402_9: pin names not known; wires that end beside it: 1'b0, n7402_2_p12, n7402_5_p2, n7402_1_p4, C, n7402_9_p6, n7402_9_p7, n7402_9_p6, n7402_9_p7, n7402_9_p6, n7402_9_p7, n7402_3_p3, n7402_6_p2, 1'b1
  // _7402 7402_10: pin names not known; wires that end beside it: 1'b0, n7402_1_p2, n7402_3_p10, A, n7402_10_p5, n7402_10_p6, n7402_10_p7, n7402_10_p6, n7402_10_p9, n7402_10_p6, n7402_10_p9, n7402_7_p8, n7402_10_p5, 1'b1
  // _7402 7402_11: pin names not known; wires that end beside it: 1'b0, n7402_1_p3, n7402_7_p6, n7402_11_p4, n7402_7_p12, n7402_4_p9, n7402_11_p7, n7402_11_p8, n7402_11_p7, n7402_11_p10, n7402_11_p7, n7402_11_p12, n7402_11_p10, 1'b1
  // _7402 7402_12: pin names not known; wires that end beside it: 1'b0, n7402_6_p12, n7402_6_p13, n7402_6_p12, n7402_6_p13, n7402_12_p6, n7402_12_p7, n7402_12_p8, n7402_12_p7, n7402_12_p8, n7402_12_p6, n7402_12_p12, n7402_12_p8, 1'b1
  // _7402 7402_13: pin names not known; wires that end beside it: 1'b0, n7402_4_p13, D, n7402_4_p13, n7402_6_p4, n7402_13_p6, n7402_13_p7, n7402_13_p6, n7402_13_p7, n7402_4_p12, n7402_13_p7, n7402_13_p12, n7402_13_p13, 1'b1, 1'b0
  // _7402 7402_14: pin names not known; wires that end beside it: 1'b0, n7402_8_p12, n7402_8_p13, n7402_8_p12, n7402_8_p13, n7402_14_p6, n7402_14_p7, n7402_14_p6, n7402_14_p7, n7402_14_p6, n7402_14_p11, n7402_14_p11, n7402_14_p13, 1'b1
  // _7402 7402_15: pin names not known; wires that end beside it: 1'b0, n7402_15_p2, n7402_3_p3, n7402_15_p2, n7402_3_p3, n7402_15_p6, n7402_15_p7, n7402_15_p8, n7402_15_p9, n7402_15_p7, n7402_15_p9, n7402_15_p2, n7402_15_p8, 1'b1
  // _7402 7402_16: pin names not known; wires that end beside it: 1'b0, n7402_1_p2, n7402_1_p3, n7402_4_p5, n7402_16_p5, n7402_16_p6, n7402_16_p7, n7402_16_p6, n7402_16_p7, n7402_16_p6, n7402_16_p7, n7402_16_p12, n7402_16_p13, 1'b1, 1'b0
  // _7402 7402_17: pin names not known; wires that end beside it: n7402_7_p8, n7402_16_p12, n7402_7_p8, n7402_16_p12, n7402_17_p5, n7402_17_p6, n7402_17_p6, n7402_16_p13, n7402_17_p9, n7402_16_p13, n7402_17_p11, n7402_17_p9, 1'b1
  // _7402 7402_18: pin names not known; wires that end beside it: n7402_13_p13, n7402_17_p5, n7402_13_p13, n7402_18_p4, n7402_18_p5, n7402_18_p6, n7402_15_p9, n7402_17_p11, n7402_15_p9, n7402_17_p11, n7402_18_p11, n7402_18_p4, 1'b1
  // _7402 7402_19: pin names not known; wires that end beside it: 1'b0, n7402_4_p5, B, n7402_11_p4, B, n7402_19_p6, n7402_4_p5, n7402_19_p6, A, n7402_19_p6, A, n7402_6_p4, n7402_11_p4, 1'b1
  // _7402 7402_20: pin names not known; wires that end beside it: 1'b0, B, B, n7402_11_p4, A, n7402_20_p6, n7402_20_p7, n7402_20_p6, n7402_20_p7, n7402_20_p6, n7402_20_p7, n7402_6_p5, n7402_1_p4, 1'b1
  // _7402 7402_21: pin names not known; wires that end beside it: 1'b0, n7402_21_p2, n7402_15_p6, n7402_21_p2, n7402_12_p12, n7402_21_p6, n7402_21_p7, n7402_21_p6, n7402_21_p9, n7402_21_p10, n7402_21_p9, n7402_10_p9, n7402_21_p10, 1'b1
  // _7402 7402_22: pin names not known; wires that end beside it: 1'b0, n7402_6_p2, n7402_2_p4, n7402_16_p5, n7402_6_p4, n7402_22_p6, n7402_22_p7, n7402_22_p6, n7402_22_p7, n7402_22_p6, n7402_22_p7, n7402_21_p9, n7402_21_p2, 1'b1
  // _7402 7402_23: pin names not known; wires that end beside it: 1'b0, n7402_2_p4, n7402_5_p2, n7402_16_p5, n7402_6_p4, n7402_23_p6, n7402_23_p7, n7402_23_p6, n7402_23_p7, n7402_23_p6, n7402_23_p7, n7402_23_p12, n7402_23_p13, 1'b1
  // _7402 7402_24: pin names not known; wires that end beside it: 1'b0, n7402_13_p12, n7402_18_p5, n7402_13_p12, n7402_18_p11, n7402_24_p6, n7402_24_p7, n7402_24_p6, n7402_24_p7, n7402_24_p10, n7402_24_p7, n7402_24_p12, n7402_24_p10, 1'b1
  // _7402 7402_25: pin names not known; wires that end beside it: 1'b0, n7402_1_p2, n7402_4_p5, n7402_6_p5, A, n7402_25_p6, n7402_25_p7, n7402_25_p6, n7402_25_p7, n7402_25_p6, n7402_25_p7, n7402_15_p9, n7402_16_p5, 1'b1
  // _7402 7402_26: pin names not known; wires that end beside it: 1'b0, n7402_26_p2, n7402_23_p12, n7402_26_p4, n7402_23_p12, n7402_26_p6, n7402_26_p2, n7402_26_p6, n7402_23_p13, n7402_26_p6, n7402_23_p13, n7402_11_p8, n7402_26_p4, 1'b1
  // _7402 7402_27: pin names not known; wires that end beside it: 1'b0, n7402_2_p12, C, B, n7402_6_p5, n7402_27_p6, n7402_27_p7, n7402_27_p6, n7402_27_p7, n7402_27_p6, n7402_27_p7, n7402_27_p12, n7402_27_p13, 1'b1
  _7_Segment_Display u_7_segment_display_1 (
    .g(n7402_14_p13), .f(n7402_24_p12), .a(n7402_21_p7), .b(n7402_11_p12), .e(n7402_29_p6), .d(n7402_10_p7),
    .c(n7402_18_p6));  // open: dp
  // _7402 7402_28: pin names not known; wires that end beside it: 1'b0, D, n7402_27_p12, n7402_11_p4, n7402_27_p12, n7402_28_p6, n7402_28_p7, n7402_28_p6, n7402_28_p6, n7402_28_p10, n7402_28_p11
  // _7402 7402_29: pin names not known; wires that end beside it: 1'b0, n7402_29_p2, n7402_28_p10, n7402_29_p4, n7402_28_p10, n7402_29_p6, n7402_29_p2, n7402_29_p8, n7402_28_p11, n7402_29_p8, n7402_28_p7, n7402_29_p4, n7402_29_p8, 1'b1

  // Notes on the sheet:
  //   (D+C’+B+A) (D+C+B+A’) 
  //   D+C'+B+A'
  //   D+C+B
  //   D’+C’+B+A
  //   D'
  //   D'+C'
  //   D+C
  //   D+C'
  //   D+C+A'
  //   D+C+B'
  //   C'
  //   D+C+B+A'
  //   D'+C+B'+A'
  //   D+C’+B'+A'
  //   D'+C
  //   D+C'+B+A
  //   D'+C'+A
  //   D+C+B'+A
  //   D'+C'+B'
  //   D+B'+A'
  //   B'
  //   B+A
  //   B+A'
  //   A'
  //   B'+A'
  //   D'+C'+B+A'
  //   C'+B'+A'
  //   D'+C+B'+A
  //   D'+B'+A'
  //   C'+B'+A
  //   B'+A
  //   C+B+A'
  //   D+C'+B
  //   D+A'
endmodule
