// Logisim project cs20labrep6c.circ as structural Verilog: 1 circuit, main circuit main
module main (
  input  A_9,
  input  A_8,
  input  A_7,
  input  A_6,
  input  A_5,
  input  A_4,
  input  A_3,
  input  A_2,
  input  A_1,
  input  A_0
);

  wire n7_segment_display_driver_1_p5, n7_segment_display_driver_1_p6, n7_segment_display_driver_1_p7,
       n7_segment_display_driver_1_p8, n7_segment_display_driver_1_p9, n7_segment_display_driver_1_p10,
       n7_segment_display_driver_1_p11, or_1_out, or_2_out, or_3_out, or_4_out, or_5_out, or_6_out, or_7_out,
       or_8_out, or_9_out, or_10_out, or_11_out;

  or or_1 (or_1_out, A_9, A_8);
  or or_2 (or_2_out, A_7, A_6);
  or or_3 (or_3_out, A_5, A_4);
  or or_4 (or_4_out, A_3, A_2);
  or or_5 (or_5_out, A_7, A_6);
  or or_6 (or_6_out, A_3, A_1);
  or or_7 (or_7_out, A_9, A_7);
  or or_8 (or_8_out, or_2_out, or_3_out);
  or or_9 (or_9_out, or_5_out, or_4_out);
  or or_10 (or_10_out, or_7_out, A_5);
  or or_11 (or_11_out, or_10_out, or_6_out);
  // _7_segment_display_driver 7_segment_display_driver_1: pin names not known; wires that end beside it: or_1_out, or_8_out, or_9_out, or_11_out, n7_segment_display_driver_1_p5, n7_segment_display_driver_1_p6, n7_segment_display_driver_1_p7, n7_segment_display_driver_1_p8, n7_segment_display_driver_1_p9, n7_segment_display_driver_1_p10, n7_segment_display_driver_1_p11
  _7_Segment_Display u_7_segment_display_1 (
    .g(n7_segment_display_driver_1_p11), .f(n7_segment_display_driver_1_p10),
    .a(n7_segment_display_driver_1_p5), .b(n7_segment_display_driver_1_p6),
    .e(n7_segment_display_driver_1_p9), .d(n7_segment_display_driver_1_p8), .c(n7_segment_display_driver_1_p7));  // open: dp
endmodule
