// Logisim project cs20lab7_1.circ as structural Verilog: 1 circuit, main circuit main
module main (
);

  wire A_out, B_out;

  Clock A (.out(A_out));
  Clock #(.highDuration(2), .lowDuration(2)) B (.out(B_out));
  LED LED_A (.in(A_out));
  LED LED_B (.in(B_out));
  // Digital_Oscilloscope digital_oscilloscope_1: pin names not known; wires that end beside it: A_out, B_out

  // Notes on the sheet:
  //   clock signal waveform
  //   generated waveform
endmodule
