// Logisim project cs20lab7_2.circ as structural Verilog: 1 circuit, main circuit main
module main (
);

  wire clock_1_out, dipswitch_1_p1, dipswitch_1_p2, j_k_ff_1_q;

  Clock #(.highDuration(3), .lowDuration(3)) clock_1 (.out(clock_1_out));
  // DipSwitch #(.NSwitches(2)) dipswitch_1: pin names not known; wires that end beside it: dipswitch_1_p1, dipswitch_1_p2
  J_K_Flip_Flop j_k_ff_1 (
    .J(dipswitch_1_p1), .clk(clock_1_out), .K(dipswitch_1_p2), .Q(j_k_ff_1_q));  // open: Qn, preset, reset
  // Digital_Oscilloscope digital_oscilloscope_1: pin names not known; wires that end beside it: clock_1_out, dipswitch_1_p1, dipswitch_1_p2, j_k_ff_1_q

  // Notes on the sheet:
  //   CLK waveform
  //   J waveform
  //   K waveform
  //   Q waveform
endmodule
