// Logisim project cs20lab8.circ as structural Verilog: 1 circuit, main circuit main
module main (
  input  x1,
  input  x2,
  output out_3,
  output out_4,
  output out_5,
  output y1,
  output y2,
  output y3
);

  wire and_1_out, and_2_out, and_3_out, and_4_out, and_5_out, and_6_out, and_7_out, and_8_out, and_9_out,
       and_10_out, and_11_out, and_12_out, and_13_out, and_14_out, and_15_out, and_16_out, and_17_out,
       and_18_out, and_19_out, and_20_out, and_21_out, and_22_out, and_23_out, and_24_out, not_1_out,
       not_2_out, or_1_out, or_2_out, or_3_out, or_4_out, or_5_out, or_6_out, or_7_out, or_8_out, or_9_out,
       or_10_out, q1_qn, q2_qn, q3_qn;

  Clock CLK (.out(out_3));
  not not_1 (not_1_out, x1);
  not not_2 (not_2_out, x2);
  and and_1 (and_1_out, x2, y1);
  and and_2 (and_2_out, x1, q1_qn);
  and and_3 (and_3_out, x1, y1);
  and and_4 (and_4_out, not_1_out, not_2_out);
  and and_5 (and_5_out, x2, y2);
  and and_6 (and_6_out, x1, q2_qn);
  and and_7 (and_7_out, not_1_out, not_2_out);
  and and_8 (and_8_out, y2, q3_qn);
  and and_9 (and_9_out, x2, q1_qn);
  and and_10 (and_10_out, x1, y1);
  and and_11 (and_11_out, not_1_out, not_2_out);
  and and_12 (and_12_out, x2, q1_qn);
  and and_13 (and_13_out, and_1_out, y2);
  and and_14 (and_14_out, and_2_out, y2);
  and and_15 (and_15_out, and_4_out, y1);
  and and_16 (and_16_out, y1, y3);
  and and_17 (and_17_out, and_5_out, q3_qn);
  and and_18 (and_18_out, and_6_out, q3_qn);
  and and_19 (and_19_out, and_7_out, y2);
  and and_20 (and_20_out, and_9_out, y3);
  and and_21 (and_21_out, and_10_out, y3);
  and and_22 (and_22_out, and_11_out, y3);
  and and_23 (and_23_out, and_12_out, q2_qn);
  or or_1 (or_1_out, and_13_out, and_14_out);
  and and_24 (and_24_out, and_3_out, q2_qn);
  or or_2 (or_2_out, and_15_out, and_16_out);
  or or_3 (or_3_out, and_17_out, and_18_out);
  or or_4 (or_4_out, and_19_out, and_8_out);
  or or_5 (or_5_out, and_20_out, and_21_out);
  or or_6 (or_6_out, and_22_out, and_23_out);
  or or_7 (or_7_out, or_1_out, and_24_out);
  or or_8 (or_8_out, or_2_out, or_3_out);
  or or_9 (or_9_out, or_4_out, or_5_out);
  or or_10 (or_10_out, or_6_out, or_7_out);
  D_Flip_Flop q1 (.clk(out_3), .D(or_8_out), .Q(y1), .Qn(q1_qn));  // open: preset, en, reset
  D_Flip_Flop q2 (.clk(out_3), .D(or_9_out), .Q(y2), .Qn(q2_qn));  // open: preset, en, reset
  D_Flip_Flop q3 (.clk(out_3), .D(or_10_out), .Q(y3), .Qn(q3_qn));  // open: preset, en, reset

  assign out_4 = x1;
  assign out_5 = x2;
endmodule
