// Logisim project mealy.circ as structural Verilog
module C2 (
  input  x1,
  input  x2,
  input  q1,
  input  q2,
  input  q3,
  output y1,
  output y2,
  output y3
);

  wire and_1_out, and_2_out, and_3_out, and_4_out, and_5_out, and_6_out, and_7_out, and_8_out, and_9_out,
       and_10_out, and_11_out, and_12_out, and_13_out, not_1_out, not_2_out, not_3_out, not_4_out, not_5_out,
       not_6_out, not_7_out, not_8_out, not_9_out, not_10_out, not_11_out, not_12_out, not_13_out,
       not_14_out, not_15_out;

  not not_1 (not_1_out, x1);
  not not_2 (not_2_out, x2);
  not not_3 (not_3_out, q3);
  not not_4 (not_4_out, q2);
  not not_5 (not_5_out, q3);
  not not_6 (not_6_out, x1);
  not not_7 (not_7_out, x2);
  not not_8 (not_8_out, q3);
  not not_9 (not_9_out, q1);
  not not_10 (not_10_out, x1);
  not not_11 (not_11_out, x2);
  not not_12 (not_12_out, q1);
  not not_13 (not_13_out, q2);
  not not_14 (not_14_out, q1);
  not not_15 (not_15_out, q2);
  and and_1 (and_1_out, not_1_out, not_2_out, q1);
  and and_2 (and_2_out, q1, q3);
  and and_3 (and_3_out, x2, q2, not_3_out);
  and and_4 (and_4_out, x1, not_4_out, not_5_out);
  and and_5 (and_5_out, not_6_out, not_7_out, q2);
  and and_6 (and_6_out, q2, not_8_out);
  and and_7 (and_7_out, x2, not_9_out, q3);
  and and_8 (and_8_out, x1, q1, q3);
  and and_9 (and_9_out, not_10_out, not_11_out, q3);
  and and_10 (and_10_out, x2, not_12_out, not_13_out);
  and and_11 (and_11_out, x2, q1, q2);
  and and_12 (and_12_out, x1, not_14_out, q2);
  and and_13 (and_13_out, x1, q1, not_15_out);
  or or_1 (y1, and_1_out, and_2_out, and_3_out, and_4_out);
  or or_2 (y2, and_5_out, and_6_out, and_7_out, and_8_out);
  or or_3 (y3, and_9_out, and_10_out, and_11_out, and_12_out, and_13_out);
endmodule
