// Logisim project cs20lab9a.circ as structural Verilog: 1 circuit, main circuit main
module main (
  output LSB,
  output MSB
);

  wire clock_1_out, d_ff_1_qn, d_ff_2_qn;

  Clock clock_1 (.out(clock_1_out));
  D_Flip_Flop d_ff_1 (.clk(clock_1_out), .D(d_ff_1_qn), .Q(LSB), .Qn(d_ff_1_qn));  // open: preset, en, reset
  D_Flip_Flop d_ff_2 (.clk(LSB), .D(d_ff_2_qn), .Q(MSB), .Qn(d_ff_2_qn));  // open: preset, en, reset
endmodule
